# Fritzing sketch valvecontroller (saved by Fritzing 0.9.3b)
breadboards: 1

parts:
  Raspberry_Pi_B_rev1 = Raspberry Pi B rev1
  S1 = Pushbutton [package="[THT]"]
  LED1 = LED - 5mm [color="Red (633nm)" package="5 mm [THT]"]
  R1 = Resistor [tolerance=±5% resistance=220 package=THT]

nets:
  N1: Raspberry_Pi_B_rev1.3V3, S1.Pin_3, S1.Pin_4
  N2: Raspberry_Pi_B_rev1.GND, R1.Pin_1
  N3: Raspberry_Pi_B_rev1.GPIO_24, LED1.anode
  N4: Raspberry_Pi_B_rev1.GPIO_25, S1.Pin_1, S1.Pin_2
  N5: LED1.cathode, R1.Pin_0
